# Fritzing sketch arduino_stoplight_v1 (saved by Fritzing 0.9.10b)
breadboards: 1

parts:
  S2 = Pushbutton [package="[THT]"]
  S3 = Pushbutton [package="[THT]"]
  S4 = Pushbutton [package="[THT]"]
  LED1 = LED - 5mm [color="Red (633nm)" current=0.030 package="5 mm [THT]"]
  Part1 = Arduino Uno (Rev3)
  LED2 = smd LED [color="Blue (430nm)" package="1206 [SMD]"]
  LED3 = smd LED [color="Yellow (595nm)" package="1206 [SMD]"]
  LED4 = smd LED [color="Green (565nm)" package="1206 [SMD]"]
  R1 = Resistor [tolerance=±5% power=0.25 resistance=220 package=THT]
  R2 = Resistor [tolerance=±5% power=0.25 resistance=220 package=THT]
  R3 = Resistor [tolerance=±5% power=0.25 resistance=220 package=THT]
  R4 = Resistor [tolerance=±5% power=0.25 resistance=220 package=THT]
  S1 = Toggle Switch [package=THT]  # not connected
  C1 = Ceramic Capacitor [capacitance=0.1µF voltage=35V package="100 mil [THT, multilayer]"]
  R5 = Resistor [tolerance=±5% power=0.25 resistance=10k package=THT]

nets:
  N1: S2.Pin_1, S2.Pin_2, Part1.D13/SCK
  N2: S2.Pin_3, S2.Pin_4, S3.Pin_3, S3.Pin_4, S4.Pin_3, S4.Pin_4, LED1.cathode, Part1.GND, LED2.anode, LED3.cathode, LED4.cathode, C1.1, R5.Pin_1
  N3: S3.Pin_1, S3.Pin_2, Part1.D12/MISO
  N4: S4.Pin_1, S4.Pin_2, Part1.D11_PWM/MOSI
  N5: LED1.anode, R1.Pin_0
  N6: Part1.D2, C1.0, R5.Pin_0
  N7: Part1.D4, R4.Pin_1
  N8: Part1.D5_PWM, R3.Pin_1
  N9: Part1.D6_PWM, R2.Pin_1
  N10: Part1.D7, R1.Pin_1
  N11: LED2.cathode, R4.Pin_0
  N12: LED3.anode, R2.Pin_0
  N13: LED4.anode, R3.Pin_0
